# Fritzing sketch Sketch (saved by Fritzing 0.8.3b)
breadboards: 2

parts:
  LCD1 = LCD screen  # not connected
  J2 = Basic Servo  # not connected
  M1 = DC Motor  # not connected
  VCC1 = 4 x AAA Battery Mount  # not connected
  Part1 = Arduino Mega 2560 (Rev3)  # not connected
  Part2 = Arduino Motor Shield (Rev3)
  J1 = Infrared Proximity Sensor
  M2 = DC Motor  # not connected

nets:
  N1: Part2.D7, J1.Vout
